// Digital circuit Project - Exp.dig as structural Verilog
module Project___Exp (
  input  Reset_Pulse
);

  wire _74154_1_p1, _74154_1_p10, _74154_1_p11, _74154_1_p12, _74154_1_p13, _74154_1_p14, _74154_2_p9,
       _74154_2_p10, _74154_2_p11, _74154_2_p12, _74154_2_p13, _74154_2_p14, Ace_Dt_nq, Ace_Dt_q, add_1_s,
       add_2_s, add_3_s, add_4_c_o, add_4_s, add_5_c_o, add_5_s, add_6_s, add_7_c_o, add_7_s, add_8_c_o,
       add_8_s, add_9_c_o, add_9_s, add_10_c_o, add_10_s, add_11_c_o, add_11_s, add_12_c_o, add_12_s,
       add_13_c_o, add_13_s, add_14_c_o, add_14_s, add_15_c_o, add_15_s, add_16_c_o, add_16_s, add_17_c_o,
       add_17_s, add_18_c_o, add_18_s, add_19_c_o, add_19_s, add_20_c_o, add_20_s, and_1_out, and_2_out,
       and_3_out, and_4_out, and_5_out, and_6_out, and_7_out, and_8_out, and_9_out, and_10_out, and_11_out,
       and_12_out, and_13_out, and_14_out, and_15_out, and_16_out, and_17_out, and_18_out, and_19_out,
       and_20_out, and_21_out, and_22_out, and_23_out, and_24_out, and_25_out, and_26_out, and_27_out,
       and_28_out, and_29_out, and_30_out, and_31_out, and_32_out, and_33_out, and_34_out, and_35_out,
       and_36_out, and_37_out, and_38_out, and_39_out, and_40_out, and_41_out, and_42_out, and_43_out,
       and_44_out, and_45_out, and_46_out, and_47_out, and_48_out, and_49_out, and_50_out, and_51_out,
       and_52_out, and_53_out, and_54_out, and_55_out, and_56_out, and_57_out, and_58_out, and_59_out,
       and_60_out, and_61_out, and_62_out, and_63_out, and_64_out, and_65_out, and_66_out, and_67_out,
       and_68_out, and_69_out, and_70_out, and_71_out, and_72_out, and_73_out, and_74_out, and_75_out,
       and_76_out, and_77_out, and_78_out, and_79_out, and_80_out, and_81_out, and_82_out, and_83_out,
       and_84_out, and_85_out, and_86_out, and_87_out, and_88_out, and_89_out, and_90_out, and_91_out,
       and_92_out, and_93_out, and_94_out, and_95_out, and_96_out, and_97_out, and_98_out, and_99_out,
       and_100_out, and_101_out, and_102_out, and_103_out, and_104_out, and_105_out, and_106_out,
       and_107_out, and_108_out, and_109_out, and_110_out, and_111_out, and_112_out, and_113_out,
       and_114_out, and_115_out, and_116_out, and_117_out, and_118_out, and_119_out, and_120_out,
       and_121_out, and_122_out, and_123_out, and_124_out, and_125_out, and_126_out, and_127_out,
       and_128_out, and_129_out, and_130_out, and_131_out, and_132_out, and_133_out, and_134_out,
       and_135_out, and_136_out, and_137_out, and_138_out, and_139_out, and_140_out, and_141_out,
       and_142_out, and_143_out, and_144_out, and_145_out, and_146_out, and_147_out, and_148_out,
       and_149_out, and_150_out, and_151_out, and_152_out, and_153_out, and_154_out, and_155_out,
       and_156_out, and_157_out, and_158_out, and_159_out, and_160_out, and_161_out, and_162_out,
       and_163_out, and_164_out, and_165_out, and_166_out, and_167_out, and_168_out, and_169_out,
       and_170_out, and_171_out, and_172_out, and_173_out, and_174_out, and_175_out, and_176_out,
       and_177_out, and_178_out, and_179_out, and_180_out, and_181_out, and_182_out, and_183_out,
       and_184_out, and_185_out, and_186_out, and_187_out, and_188_out, and_189_out, and_190_out,
       and_191_out, and_192_out, and_193_out, and_194_out, and_195_out, and_196_out, and_197_out,
       and_198_out, and_199_out, and_200_out, and_201_out, and_202_out, and_203_out, and_204_out, C_0_1_p14,
       C_0_1_p15, C_0_1_p16, C_0_2_p14, C_0_2_p15, C_0_2_p16, C_0_3_p14, C_0_3_p15, C_0_3_p16, C_0_4_p14,
       C_0_4_p15, C_0_4_p16, C_1_2_p14, C_1_2_p15, C_1_2_p16, C_1_3_p14, C_1_3_p15, C_1_3_p16, C_1_4_p14,
       C_1_4_p15, C_1_4_p16, C_2_3_p14, C_2_3_p15, C_2_3_p16, C_2_4_p14, C_2_4_p15, C_2_4_p16, C_3_4_p14,
       C_3_4_p15, C_3_4_p16, D0_0_2_q, D0_0_q, D0_1_q, D0_2_q, D0_3_q, D0_4_q, D0_out, D1_0_2_q, D1_0_q,
       D1_1_q, D1_2_q, D1_3_q, D1_4_q, D1_out, D2_0_2_q, D2_0_q, D2_1_q, D2_2_q, D2_3_q, D2_4_q, D2_out,
       D3_0_2_q, D3_0_q, D3_1_q, D3_2_q, D3_3_q, D3_4_q, D3_out, d_ff_1_nq, d_ff_1_q, d_ff_2_q, d_ff_3_q,
       d_ff_4_q, d_ff_5_nq, d_ff_5_q, nor_1_out, nor_2_out, not_1_out, not_2_out, not_3_out, not_4_out,
       not_5_out, not_6_out, not_7_out, not_8_out, not_9_out, not_10_out, not_11_out, not_12_out, not_13_out,
       not_14_out, not_15_out, not_16_out, not_17_out, not_18_out, not_19_out, not_20_out, not_21_out,
       not_22_out, or_1_out, or_2_out, or_3_out, or_4_out, or_5_out, or_6_out, or_7_out, or_8_out, or_9_out,
       or_10_out, or_11_out, or_12_out, or_13_out, or_14_out, or_15_out, or_16_out, or_17_out, or_18_out,
       or_19_out, or_20_out, or_21_out, or_22_out, or_23_out, or_24_out, or_25_out, or_26_out, or_27_out,
       or_28_out, or_29_out, or_30_out, or_31_out, or_32_out, or_33_out, or_34_out, or_35_out, or_36_out,
       or_37_out, or_38_out, or_39_out, or_40_out, or_41_out, or_42_out, or_43_out, or_44_out, P0_out,
       P1_out, P2_out, P3_out, Reset_out, Store_out, xor_1_out;

  DipSwitch P3 (.out(P3_out));
  DipSwitch P2 (.out(P2_out));
  DipSwitch P1 (.out(P1_out));
  DipSwitch P0 (.out(P0_out));
  DipSwitch D3 (.out(D3_out));
  DipSwitch D2 (.out(D2_out));
  DipSwitch D1 (.out(D1_out));
  DipSwitch D0 (.out(D0_out));
  Button Store (.out(Store_out));
  Button Reset (.out(Reset_out));
  LED Soft_Total (.in(Ace_Dt_q));
  LED Split (.in(or_44_out));
  LED Hit (.in(or_12_out));
  LED Stand (.in(or_13_out));
  LED Double (.in(or_14_out));
  LED Surrender (.in(or_17_out));
  Seven_Seg seven_seg_1 (
    .a(or_24_out), .b(or_25_out), .c(or_26_out), .d(or_27_out), .e(or_28_out), .f(or_29_out),
    .g(and_114_out), .dp(1'b0));
  Seven_Seg seven_seg_2 (
    .a(or_32_out), .b(or_33_out), .c(or_30_out), .d(or_34_out), .e(or_31_out), .f(or_35_out), .g(or_36_out),
    .dp(1'b0));
  // _74154 _74154_1: pin names not known; wires that end beside it: _74154_1_p1, D0_out, D2_out, D1_out, D3_out, 1'b0, 1'b0, 1'b1, 1'b0, _74154_1_p10, _74154_1_p11, _74154_1_p12, _74154_1_p13, _74154_1_p14
  // _74154 _74154_2: pin names not known; wires that end beside it: P0_out, P2_out, P1_out, P3_out, 1'b0, 1'b0, 1'b1, 1'b0, _74154_2_p9, _74154_2_p10, _74154_2_p11, _74154_2_p12, _74154_2_p13, _74154_2_p14
  and and_1 (and_1_out, _74154_1_p1, _74154_1_p10, _74154_1_p11, _74154_1_p12, _74154_1_p13, _74154_1_p14);
  or or_1 (or_1_out, and_1_out, or_2_out);
  and and_2 (and_2_out, _74154_2_p10, _74154_2_p11, _74154_2_p12, _74154_2_p13, _74154_2_p14, _74154_2_p9);
  and and_3 (and_3_out, and_2_out, Store_out, or_1_out);
  and and_4 (and_4_out, Reset_Pulse, nor_2_out, Reset_out, nor_1_out);
  nor nor_1 (nor_1_out, D0_out, D1_out, D2_out, D3_out);
  nor nor_2 (nor_2_out, P0_out, P1_out, P2_out, P3_out);
  or or_2 (or_2_out, D0_0_2_q, D1_0_2_q, D2_0_2_q, D3_0_2_q);
  or or_3 (or_3_out, and_4_out, and_3_out);
  and and_5 (and_5_out, d_ff_1_nq, and_3_out);
  and and_6 (and_6_out, and_3_out, d_ff_5_nq);
  D_FF d_ff_1 (.D(and_3_out), .C(or_3_out), .Q(d_ff_1_q), .nQ(d_ff_1_nq));
  or or_4 (or_4_out, Reset_out, and_5_out);
  or or_5 (or_5_out, and_4_out, and_6_out);
  Register D3_0 (.D(P3_out), .C(or_5_out), .en(or_5_out), .Q(D3_0_q));
  Register D2_0 (.D(P2_out), .C(or_5_out), .en(or_5_out), .Q(D2_0_q));
  Register D1_0 (.D(P1_out), .C(or_5_out), .en(or_5_out), .Q(D1_0_q));
  Register D0_0 (.D(P0_out), .C(or_5_out), .en(or_5_out), .Q(D0_0_q));
  D_FF d_ff_2 (.D(d_ff_1_q), .C(or_3_out), .Q(d_ff_2_q));  // open: nQ
  Register D3_0_2 (.D(D3_out), .C(or_4_out), .en(or_4_out), .Q(D3_0_2_q));
  Register D2_0_2 (.D(D2_out), .C(or_4_out), .en(or_4_out), .Q(D2_0_2_q));
  Register D1_0_2 (.D(D1_out), .C(or_4_out), .en(or_4_out), .Q(D1_0_2_q));
  Register D0_0_2 (.D(D0_out), .C(or_4_out), .en(or_4_out), .Q(D0_0_2_q));
  D_FF d_ff_3 (.D(d_ff_2_q), .C(or_3_out), .Q(d_ff_3_q));  // open: nQ
  or or_6 (or_6_out, D3_0_q, D2_0_q, D1_0_q, D0_0_q);
  Register D3_1 (.D(D3_0_q), .C(or_5_out), .en(or_5_out), .Q(D3_1_q));
  Register D2_1 (.D(D2_0_q), .C(or_5_out), .en(or_5_out), .Q(D2_1_q));
  Register D1_1 (.D(D1_0_q), .C(or_5_out), .en(or_5_out), .Q(D1_1_q));
  Register D0_1 (.D(D0_0_q), .C(or_5_out), .en(or_5_out), .Q(D0_1_q));
  D_FF d_ff_4 (.D(d_ff_3_q), .C(or_3_out), .Q(d_ff_4_q));  // open: nQ
  D_FF d_ff_5 (.D(d_ff_4_q), .C(or_3_out), .Q(d_ff_5_q), .nQ(d_ff_5_nq));
  or or_7 (or_7_out, D3_1_q, D2_1_q, D1_1_q, D0_1_q);
  Register D3_2 (.D(D3_1_q), .C(or_5_out), .en(or_5_out), .Q(D3_2_q));
  Register D2_2 (.D(D2_1_q), .C(or_5_out), .en(or_5_out), .Q(D2_2_q));
  Register D1_2 (.D(D1_1_q), .C(or_5_out), .en(or_5_out), .Q(D1_2_q));
  Register D0_2 (.D(D0_1_q), .C(or_5_out), .en(or_5_out), .Q(D0_2_q));
  or or_8 (or_8_out, D3_2_q, D2_2_q, D1_2_q, D0_2_q);
  Register D3_3 (.D(D3_2_q), .C(or_5_out), .en(or_5_out), .Q(D3_3_q));
  Register D2_3 (.D(D2_2_q), .C(or_5_out), .en(or_5_out), .Q(D2_3_q));
  Register D1_3 (.D(D1_2_q), .C(or_5_out), .en(or_5_out), .Q(D1_3_q));
  Register D0_3 (.D(D0_2_q), .C(or_5_out), .en(or_5_out), .Q(D0_3_q));
  or or_9 (or_9_out, and_4_out, and_3_out);
  Register D3_4 (.D(D3_3_q), .C(or_5_out), .en(or_5_out), .Q(D3_4_q));
  Register D2_4 (.D(D2_3_q), .C(or_5_out), .en(or_5_out), .Q(D2_4_q));
  Register D1_4 (.D(D1_3_q), .C(or_5_out), .en(or_5_out), .Q(D1_4_q));
  Register D0_4 (.D(D0_3_q), .C(or_5_out), .en(or_5_out), .Q(D0_4_q));
  or or_10 (or_10_out, D3_3_q, D2_3_q, D1_3_q, D0_3_q);
  and and_7 (and_7_out, ~D3_4_q, ~D2_4_q, ~D1_4_q, D0_4_q);  // And
  and and_8 (and_8_out, ~D3_3_q, ~D2_3_q, ~D1_3_q, D0_3_q);  // And
  and and_9 (and_9_out, ~D3_2_q, ~D2_2_q, ~D1_2_q, D0_2_q);  // And
  and and_10 (and_10_out, ~D3_1_q, ~D2_1_q, ~D1_1_q, D0_1_q);  // And
  and and_11 (and_11_out, ~D3_0_q, ~D2_0_q, ~D1_0_q, D0_0_q);  // And
  // _7485 C_0_1: pin names not known; wires that end beside it: 1'b0, or_6_out, 1'b0, D0_0_q, D1_0_q, D2_0_q, D3_0_q, D0_1_q, D1_1_q, D2_1_q, D3_1_q, 1'b1, 1'b0, C_0_1_p14, C_0_1_p15, C_0_1_p16, C_0_1_p14, C_0_1_p16
  // _7485 C_0_2: pin names not known; wires that end beside it: 1'b0, or_6_out, 1'b0, D0_0_q, D1_0_q, D2_0_q, D3_0_q, D0_2_q, D1_2_q, D2_2_q, D3_2_q, 1'b1, 1'b0, C_0_2_p14, C_0_2_p15, C_0_2_p16, C_0_2_p14, C_0_2_p16
  // _7485 C_0_3: pin names not known; wires that end beside it: 1'b0, or_6_out, 1'b0, D0_0_q, D1_0_q, D2_0_q, D3_0_q, D0_3_q, D1_3_q, D2_3_q, D3_3_q, 1'b1, 1'b0, C_0_3_p14, C_0_3_p15, C_0_3_p16, C_0_3_p14, C_0_3_p16
  // _7485 C_0_4: pin names not known; wires that end beside it: 1'b0, or_6_out, 1'b0, D0_0_q, D1_0_q, D2_0_q, D3_0_q, D0_4_q, D1_4_q, D2_4_q, D3_4_q, 1'b1, 1'b0, C_0_4_p14, C_0_4_p15, C_0_4_p16, C_0_4_p14, C_0_4_p16
  // _7485 C_1_2: pin names not known; wires that end beside it: 1'b0, or_7_out, 1'b0, D0_1_q, D1_1_q, D2_1_q, D3_1_q, D0_2_q, D1_2_q, D2_2_q, D3_2_q, 1'b1, 1'b0, C_1_2_p14, C_1_2_p15, C_1_2_p16, C_1_2_p14, C_1_2_p16
  // _7485 C_1_3: pin names not known; wires that end beside it: 1'b0, or_7_out, 1'b0, D0_1_q, D1_1_q, D2_1_q, D3_1_q, D0_3_q, D1_3_q, D2_3_q, D3_3_q, 1'b1, 1'b0, C_1_3_p14, C_1_3_p15, C_1_3_p16, C_1_3_p14, C_1_3_p16
  // _7485 C_1_4: pin names not known; wires that end beside it: 1'b0, or_7_out, 1'b0, D0_1_q, D1_1_q, D2_1_q, D3_1_q, D0_4_q, D1_4_q, D2_4_q, D3_4_q, 1'b1, 1'b0, C_1_4_p14, C_1_4_p15, C_1_4_p16, C_1_4_p14, C_1_4_p16
  // _7485 C_2_3: pin names not known; wires that end beside it: 1'b0, or_8_out, 1'b0, D0_2_q, D1_2_q, D2_2_q, D3_2_q, D0_3_q, D1_3_q, D2_3_q, D3_3_q, 1'b1, 1'b0, C_2_3_p14, C_2_3_p15, C_2_3_p16, C_2_3_p14, C_2_3_p16
  // _7485 C_2_4: pin names not known; wires that end beside it: 1'b0, or_8_out, 1'b0, D0_2_q, D1_2_q, D2_2_q, D3_2_q, D0_4_q, D1_4_q, D2_4_q, D3_4_q, 1'b1, 1'b0, C_2_4_p14, C_2_4_p15, C_2_4_p16, C_2_4_p14, C_2_4_p16
  // _7485 C_3_4: pin names not known; wires that end beside it: 1'b0, or_10_out, 1'b0, D0_3_q, D1_3_q, D2_3_q, D3_3_q, D0_4_q, D1_4_q, D2_4_q, D3_4_q, 1'b1, 1'b0, C_3_4_p14, C_3_4_p15, C_3_4_p16, C_3_4_p14, C_3_4_p16
  or or_11 (or_11_out, and_7_out, and_8_out, and_9_out, and_10_out, and_11_out);
  D_FF Ace_Dt (.D(or_11_out), .C(~or_9_out), .Q(Ace_Dt_q), .nQ(Ace_Dt_nq));
  not not_1 (not_1_out, add_1_s);
  Add add_1 (.a(1'b0), .b(add_2_s), .c_i(add_4_c_o), .s(add_1_s));  // open: c_o
  not not_2 (not_2_out, add_4_s);
  Add add_2 (.a(1'b0), .b(add_3_s), .c_i(add_5_c_o), .s(add_2_s));  // open: c_o
  not not_3 (not_3_out, add_8_s);
  not not_4 (not_4_out, add_12_s);
  Add add_3 (.a(1'b0), .b(add_6_s), .c_i(add_7_c_o), .s(add_3_s));  // open: c_o
  Add add_4 (.a(D3_4_q), .b(add_5_s), .c_i(add_8_c_o), .s(add_4_s), .c_o(add_4_c_o));
  not not_5 (not_5_out, add_16_s);
  Add add_5 (.a(D3_3_q), .b(add_7_s), .c_i(add_9_c_o), .s(add_5_s), .c_o(add_5_c_o));
  not not_6 (not_6_out, D3_0_2_q);
  Add add_6 (.a(1'b0), .b(1'b0), .c_i(add_10_c_o), .s(add_6_s));  // open: c_o
  Add add_7 (.a(D3_2_q), .b(add_10_s), .c_i(add_11_c_o), .s(add_7_s), .c_o(add_7_c_o));
  Add add_8 (.a(D2_4_q), .b(add_9_s), .c_i(add_12_c_o), .s(add_8_s), .c_o(add_8_c_o));
  not not_7 (not_7_out, D2_0_2_q);
  not not_8 (not_8_out, D1_0_2_q);
  Add add_9 (.a(D2_3_q), .b(add_11_s), .c_i(add_13_c_o), .s(add_9_s), .c_o(add_9_c_o));
  not not_9 (not_9_out, D0_0_2_q);
  Add add_10 (.a(D3_1_q), .b(D3_0_q), .c_i(add_14_c_o), .s(add_10_s), .c_o(add_10_c_o));
  Add add_11 (.a(D2_2_q), .b(add_14_s), .c_i(add_15_c_o), .s(add_11_s), .c_o(add_11_c_o));
  Add add_12 (.a(D1_4_q), .b(add_13_s), .c_i(add_16_c_o), .s(add_12_s), .c_o(add_12_c_o));
  and and_12 (and_12_out, D0_0_2_q, not_8_out, not_7_out, Ace_Dt_nq, add_4_s, not_1_out);
  and and_13 (and_13_out, not_9_out, not_7_out, D3_0_2_q, Ace_Dt_nq, add_4_s, not_1_out);
  and and_14 (and_14_out, D0_0_2_q, not_8_out, not_7_out, Ace_Dt_q, add_16_s, add_12_s, not_2_out, not_1_out);
  and and_15 (and_15_out, not_9_out, D1_0_2_q, not_7_out, Ace_Dt_q, add_16_s, add_12_s, not_2_out, not_1_out);
  and and_16 (and_16_out, D0_0_2_q, not_8_out, not_7_out, Ace_Dt_nq, add_16_s, add_8_s, not_1_out);
  and and_17 (and_17_out, D0_0_2_q, not_8_out, not_7_out, Ace_Dt_nq, add_12_s, add_8_s, not_1_out);
  and and_18 (and_18_out, D0_0_2_q, not_8_out, not_7_out, Ace_Dt_q, add_8_s, not_2_out, not_1_out);
  and and_19 (and_19_out, not_9_out, D1_0_2_q, not_7_out, Ace_Dt_q, add_8_s, not_2_out, not_1_out);
  and and_20 (and_20_out, not_9_out, not_7_out, D3_0_2_q, Ace_Dt_nq, add_16_s, add_8_s, not_1_out);
  and and_21 (and_21_out, not_9_out, not_7_out, D3_0_2_q, Ace_Dt_nq, add_12_s, add_8_s, not_1_out);
  and and_22 (and_22_out, D0_0_2_q, D1_0_2_q, D2_0_2_q, not_6_out, Ace_Dt_nq, not_5_out, not_4_out, not_3_out, not_2_out, add_1_s);
  and and_23 (and_23_out, D0_0_2_q, not_8_out, not_7_out, Ace_Dt_nq, not_5_out, not_4_out, not_3_out, not_2_out, add_1_s);
  and and_24 (and_24_out, not_9_out, not_7_out, D3_0_2_q, Ace_Dt_nq, not_5_out, not_4_out, not_3_out, not_2_out, add_1_s);
  and and_25 (and_25_out, D0_0_2_q, not_8_out, not_7_out, D3_0_2_q, not_5_out, not_4_out, not_3_out, add_4_s, not_1_out);
  and and_26 (and_26_out, not_9_out, D1_0_2_q, not_7_out, D3_0_2_q, not_5_out, not_4_out, not_3_out, add_4_s, not_1_out);
  and and_27 (and_27_out, not_9_out, not_7_out, D3_0_2_q, Ace_Dt_q, add_16_s, add_12_s, not_2_out, not_1_out);
  and and_28 (and_28_out, D0_0_2_q, D1_0_2_q, D2_0_2_q, not_6_out, Ace_Dt_nq, add_4_s, not_1_out);
  and and_29 (and_29_out, not_9_out, not_7_out, D3_0_2_q, Ace_Dt_q, add_8_s, not_2_out, not_1_out);
  and and_30 (and_30_out, D0_0_2_q, not_6_out, Ace_Dt_q, add_16_s, add_12_s, not_2_out, not_1_out);
  and and_31 (and_31_out, D0_0_2_q, not_6_out, Ace_Dt_q, add_8_s, not_2_out, not_1_out);
  and and_32 (and_32_out, D1_0_2_q, not_7_out, not_6_out, Ace_Dt_nq, not_5_out, not_4_out, add_4_s, not_1_out);
  and and_33 (and_33_out, D1_0_2_q, not_6_out, Ace_Dt_nq, not_3_out, add_4_s, not_1_out);
  and and_34 (and_34_out, D1_0_2_q, not_6_out, add_16_s, add_8_s, not_2_out, not_1_out);
  and and_35 (and_35_out, D1_0_2_q, not_6_out, add_12_s, add_8_s, not_2_out, not_1_out);
  and and_36 (and_36_out, D2_0_2_q, not_6_out, Ace_Dt_q, add_16_s, add_12_s, not_2_out, not_1_out);
  and and_37 (and_37_out, D2_0_2_q, not_6_out, Ace_Dt_q, add_8_s, not_2_out, not_1_out);
  and and_38 (and_38_out, D2_0_2_q, not_6_out, Ace_Dt_nq, not_3_out, add_4_s, not_1_out);
  and and_39 (and_39_out, D2_0_2_q, not_6_out, add_16_s, add_8_s, not_2_out, not_1_out);
  and and_40 (and_40_out, D2_0_2_q, not_6_out, add_12_s, add_8_s, not_2_out, not_1_out);
  and and_41 (and_41_out, D0_0_2_q, not_6_out, Ace_Dt_nq, add_12_s, not_3_out, not_2_out, add_1_s);
  and and_42 (and_42_out, D0_0_2_q, not_6_out, Ace_Dt_nq, not_4_out, add_8_s, not_2_out, add_1_s);
  and and_43 (and_43_out, not_9_out, D1_0_2_q, not_6_out, Ace_Dt_nq, not_4_out, not_2_out, add_1_s);
  and and_44 (and_44_out, not_9_out, D1_0_2_q, not_7_out, Ace_Dt_nq, add_12_s, not_3_out, not_2_out, add_1_s);
  and and_45 (and_45_out, not_9_out, not_7_out, D3_0_2_q, Ace_Dt_nq, not_4_out, add_8_s, not_2_out, add_1_s);
  and and_46 (and_46_out, not_9_out, D2_0_2_q, not_6_out, Ace_Dt_nq, not_3_out, not_2_out, add_1_s);
  and and_47 (and_47_out, not_9_out, D1_0_2_q, not_7_out, Ace_Dt_q, add_16_s, not_4_out, not_3_out, add_4_s, not_1_out);
  and and_48 (and_48_out, not_9_out, D1_0_2_q, not_7_out, Ace_Dt_q, not_5_out, add_12_s, not_3_out, add_4_s, not_1_out);
  and and_49 (and_49_out, not_9_out, not_8_out, not_7_out, D3_0_2_q, Ace_Dt_q, not_3_out, add_4_s, not_1_out);
  and and_50 (and_50_out, D0_0_2_q, not_8_out, not_7_out, Ace_Dt_nq, add_16_s, not_4_out, not_2_out, add_1_s);
  and and_51 (and_51_out, D0_0_2_q, not_8_out, not_7_out, Ace_Dt_q, add_16_s, not_3_out, add_4_s, not_1_out);
  and and_52 (and_52_out, D0_0_2_q, not_8_out, not_7_out, Ace_Dt_q, add_12_s, not_3_out, add_4_s, not_1_out);
  and and_53 (and_53_out, D0_0_2_q, not_8_out, not_7_out, Ace_Dt_nq, not_4_out, add_8_s, not_2_out, add_1_s);
  and and_54 (and_54_out, not_9_out, not_7_out, D3_0_2_q, Ace_Dt_nq, add_16_s, not_4_out, not_2_out, add_1_s);
  and and_55 (and_55_out, not_9_out, D2_0_2_q, not_6_out, Ace_Dt_nq, add_8_s, add_4_s, not_1_out);
  and and_56 (and_56_out, D0_0_2_q, not_6_out, Ace_Dt_nq, add_16_s, not_4_out, not_2_out, add_1_s);
  and and_57 (and_57_out, D0_0_2_q, not_6_out, Ace_Dt_q, not_3_out, add_4_s, not_1_out);
  and and_58 (and_58_out, not_8_out, not_7_out, D3_0_2_q, Ace_Dt_nq, add_12_s, not_3_out, not_2_out, add_1_s);
  and and_59 (and_59_out, not_8_out, D2_0_2_q, not_6_out, Ace_Dt_nq, not_4_out, not_2_out, add_1_s);
  and and_60 (and_60_out, D1_0_2_q, not_7_out, not_6_out, Ace_Dt_nq, add_16_s, add_8_s, add_4_s, not_1_out);
  and and_61 (and_61_out, D1_0_2_q, not_7_out, not_6_out, Ace_Dt_nq, add_12_s, add_8_s, add_4_s, not_1_out);
  and and_62 (and_62_out, D1_0_2_q, not_7_out, not_6_out, Ace_Dt_nq, not_4_out, not_2_out, add_1_s);
  and and_63 (and_63_out, not_8_out, D2_0_2_q, not_6_out, Ace_Dt_nq, add_8_s, add_4_s, not_1_out);
  and and_64 (and_64_out, D1_0_2_q, not_6_out, Ace_Dt_q, not_3_out, add_4_s, not_1_out);
  and and_65 (and_65_out, D2_0_2_q, not_6_out, Ace_Dt_q, not_3_out, add_4_s, not_1_out);
  and and_66 (and_66_out, D0_0_2_q, D1_0_2_q, not_7_out, not_6_out, Ace_Dt_q, not_5_out, not_4_out, not_3_out, add_4_s, not_1_out);
  and and_67 (and_67_out, D0_0_2_q, not_8_out, not_7_out, Ace_Dt_nq, add_16_s, add_12_s, not_3_out, add_4_s, not_1_out);
  and and_68 (and_68_out, not_9_out, D1_0_2_q, not_7_out, Ace_Dt_nq, add_16_s, add_12_s, not_3_out, add_4_s, not_1_out);
  and and_69 (and_69_out, D0_0_2_q, not_8_out, D2_0_2_q, not_6_out, not_5_out, not_4_out, not_3_out, add_4_s, not_1_out);
  and and_70 (and_70_out, not_9_out, D2_0_2_q, not_6_out, Ace_Dt_q, add_16_s, add_12_s, not_2_out, not_1_out);
  and and_71 (and_71_out, not_9_out, D1_0_2_q, D2_0_2_q, not_6_out, not_4_out, not_3_out, add_4_s, not_1_out);
  and and_72 (and_72_out, not_9_out, D2_0_2_q, not_6_out, Ace_Dt_q, add_8_s, not_2_out, not_1_out);
  and and_73 (and_73_out, D1_0_2_q, not_7_out, not_6_out, Ace_Dt_q, add_16_s, add_12_s, add_8_s, not_2_out, not_1_out);
  and and_74 (and_74_out, not_8_out, D2_0_2_q, not_6_out, Ace_Dt_q, not_5_out, not_4_out, not_3_out, add_4_s, not_1_out);
  and and_75 (and_75_out, not_8_out, D2_0_2_q, not_6_out, Ace_Dt_q, add_16_s, add_12_s, not_2_out, not_1_out);
  and and_76 (and_76_out, D1_0_2_q, not_7_out, not_6_out, Ace_Dt_nq, add_16_s, not_3_out, add_4_s, not_1_out);
  and and_77 (and_77_out, not_8_out, D2_0_2_q, not_6_out, Ace_Dt_nq, add_16_s, not_3_out, add_4_s, not_1_out);
  and and_78 (and_78_out, not_8_out, not_7_out, D3_0_2_q, Ace_Dt_nq, add_12_s, not_3_out, add_4_s, not_1_out);
  and and_79 (and_79_out, not_8_out, D2_0_2_q, not_6_out, Ace_Dt_q, add_8_s, not_2_out, not_1_out);
  and and_80 (and_80_out, D1_0_2_q, not_6_out, Ace_Dt_nq, add_12_s, not_3_out, add_4_s, not_1_out);
  and and_81 (and_81_out, D2_0_2_q, not_6_out, Ace_Dt_nq, add_12_s, not_3_out, add_4_s, not_1_out);
  and and_82 (and_82_out, D0_0_2_q, not_8_out, not_7_out, not_6_out, Ace_Dt_nq, not_5_out, not_4_out, not_3_out, not_2_out, add_1_s);
  and and_83 (and_83_out, not_9_out, D1_0_2_q, not_7_out, D3_0_2_q, Ace_Dt_nq, not_5_out, not_4_out, not_3_out, not_2_out, add_1_s);
  Add add_13 (.a(D1_3_q), .b(add_15_s), .c_i(add_17_c_o), .s(add_13_s), .c_o(add_13_c_o));
  Add add_14 (.a(D2_1_q), .b(D2_0_q), .c_i(add_18_c_o), .s(add_14_s), .c_o(add_14_c_o));
  Add add_15 (.a(D1_2_q), .b(add_18_s), .c_i(add_19_c_o), .s(add_15_s), .c_o(add_15_c_o));
  Add add_16 (.a(D0_4_q), .b(add_17_s), .c_i(1'b0), .s(add_16_s), .c_o(add_16_c_o));
  or or_12 (or_12_out, and_84_out, or_43_out);
  or or_13 (or_13_out, and_85_out, or_41_out);
  or or_14 (or_14_out, and_86_out, or_42_out);
  or or_15 (or_15_out, and_82_out, and_83_out);
  or or_16 (or_16_out, C_3_4_p15, C_2_4_p15, C_2_3_p15, C_1_4_p15, C_1_3_p15, C_1_2_p15, C_0_4_p15, C_0_3_p15, C_0_2_p15, C_0_1_p15);
  Add add_17 (.a(D0_3_q), .b(add_19_s), .c_i(1'b0), .s(add_17_s), .c_o(add_17_c_o));
  or or_17 (or_17_out, and_87_out, and_191_out);
  or or_18 (or_18_out, and_66_out, and_67_out, and_68_out, and_69_out, and_70_out, and_71_out, and_72_out, and_73_out, and_74_out, and_75_out, and_76_out, and_77_out, and_78_out, and_79_out, and_80_out, and_81_out);
  or or_19 (or_19_out, C_0_1_p15, C_0_2_p15, C_0_3_p15, C_0_4_p15);
  or or_20 (or_20_out, C_1_2_p15, C_1_3_p15, C_1_4_p15);
  or or_21 (or_21_out, C_2_3_p15, C_2_4_p15);
  Add add_18 (.a(D1_1_q), .b(D1_0_q), .c_i(add_20_c_o), .s(add_18_s), .c_o(add_18_c_o));
  Add add_19 (.a(D0_2_q), .b(add_20_s), .c_i(1'b0), .s(add_19_s), .c_o(add_19_c_o));
  and and_84 (and_84_out, or_23_out, xor_1_out);
  and and_85 (and_85_out, or_22_out, xor_1_out);
  and and_86 (and_86_out, or_18_out, xor_1_out);
  or or_22 (or_22_out, and_41_out, and_42_out, and_43_out, and_44_out, and_45_out, and_46_out, and_47_out, and_48_out, and_49_out, and_50_out, and_51_out, and_52_out, and_53_out, and_54_out, and_55_out, and_56_out, and_57_out, and_58_out, and_59_out, and_60_out, and_61_out, and_62_out, and_63_out, and_64_out, and_65_out);
  and and_87 (and_87_out, or_15_out, xor_1_out);
  or or_23 (or_23_out, and_12_out, and_13_out, and_14_out, and_15_out, and_16_out, and_17_out, and_18_out, and_19_out, and_20_out, and_21_out, and_22_out, and_23_out, and_24_out, and_25_out, and_26_out, and_27_out, and_28_out, and_29_out, and_30_out, and_31_out, and_32_out, and_33_out, and_34_out, and_35_out, and_36_out, and_37_out, and_38_out, and_39_out, and_40_out);
  Add add_20 (.a(D0_1_q), .b(D0_0_q), .c_i(1'b0), .s(add_20_s), .c_o(add_20_c_o));
  not not_10 (not_10_out, add_1_s);
  not not_11 (not_11_out, add_4_s);
  not not_12 (not_12_out, add_8_s);
  not not_13 (not_13_out, add_12_s);
  not not_14 (not_14_out, add_16_s);
  and and_88 (and_88_out, add_16_s, not_13_out, not_12_out, not_10_out);
  and and_89 (and_89_out, not_13_out, not_12_out, add_4_s, not_10_out);
  and and_90 (and_90_out, not_13_out, add_8_s, not_11_out);
  and and_91 (and_91_out, add_12_s, not_11_out, not_10_out);
  and and_92 (and_92_out, add_16_s, not_13_out, not_11_out);
  and and_93 (and_93_out, not_13_out, add_8_s, not_11_out);
  and and_94 (and_94_out, add_12_s, not_10_out);
  and and_95 (and_95_out, not_12_out, not_11_out, add_1_s);
  and and_96 (and_96_out, add_4_s, not_10_out);
  and and_97 (and_97_out, add_16_s, not_12_out, not_11_out);
  and and_98 (and_98_out, add_12_s, not_12_out, not_11_out);
  and and_99 (and_99_out, not_12_out, not_11_out, add_1_s);
  and and_100 (and_100_out, add_8_s, not_10_out);
  and and_101 (and_101_out, add_4_s, not_10_out);
  and and_102 (and_102_out, add_16_s, not_13_out, not_12_out, not_10_out);
  and and_103 (and_103_out, not_13_out, not_12_out, add_4_s, not_10_out);
  and and_104 (and_104_out, not_13_out, add_8_s, not_11_out);
  and and_105 (and_105_out, add_12_s, not_11_out, not_10_out);
  and and_106 (and_106_out, add_16_s, not_13_out, not_12_out, not_10_out);
  and and_107 (and_107_out, not_13_out, not_12_out, add_4_s, not_10_out);
  and and_108 (and_108_out, not_13_out, add_8_s, not_11_out);
  and and_109 (and_109_out, add_12_s, not_11_out, not_10_out);
  and and_110 (and_110_out, add_16_s, not_13_out, not_12_out, not_10_out);
  and and_111 (and_111_out, not_13_out, not_12_out, add_4_s, not_10_out);
  and and_112 (and_112_out, add_12_s, not_11_out, not_10_out);
  and and_113 (and_113_out, add_8_s, not_11_out, not_10_out);
  and and_114 (and_114_out, not_13_out, add_8_s, not_11_out, add_1_s);
  and and_115 (and_115_out, not_14_out, add_12_s, not_12_out, not_10_out);
  and and_116 (and_116_out, not_14_out, not_13_out, not_11_out, add_1_s);
  and and_117 (and_117_out, add_16_s, add_8_s, not_10_out);
  and and_118 (and_118_out, add_12_s, not_11_out, not_10_out);
  and and_119 (and_119_out, not_13_out, add_4_s, not_10_out);
  and and_120 (and_120_out, not_12_out, not_11_out, add_1_s);
  and and_121 (and_121_out, not_14_out, not_13_out, add_8_s, not_11_out);
  and and_122 (and_122_out, add_16_s, add_12_s, not_11_out, not_10_out);
  and and_123 (and_123_out, add_16_s, not_13_out, not_11_out, add_1_s);
  and and_124 (and_124_out, add_16_s, not_12_out, not_10_out);
  and and_125 (and_125_out, not_14_out, add_4_s, not_10_out);
  and and_126 (and_126_out, add_12_s, not_12_out, not_11_out);
  and and_127 (and_127_out, not_13_out, add_4_s, not_10_out);
  and and_128 (and_128_out, add_16_s, not_10_out);
  and and_129 (and_129_out, not_13_out, add_8_s, not_11_out);
  and and_130 (and_130_out, add_12_s, add_8_s, not_10_out);
  and and_131 (and_131_out, not_12_out, add_4_s, not_10_out);
  and and_132 (and_132_out, not_12_out, not_11_out, add_1_s);
  and and_133 (and_133_out, not_14_out, add_12_s, not_12_out, not_11_out);
  and and_134 (and_134_out, add_16_s, not_13_out, add_8_s, not_10_out);
  and and_135 (and_135_out, not_14_out, add_12_s, not_11_out, not_10_out);
  and and_136 (and_136_out, not_14_out, not_13_out, add_4_s, not_10_out);
  and and_137 (and_137_out, not_14_out, not_13_out, not_11_out, add_1_s);
  and and_138 (and_138_out, not_14_out, not_12_out, add_4_s, not_10_out);
  and and_139 (and_139_out, add_16_s, add_8_s, add_4_s, not_10_out);
  and and_140 (and_140_out, add_12_s, not_12_out, not_11_out, not_10_out);
  and and_141 (and_141_out, not_14_out, add_12_s, not_12_out, not_11_out);
  and and_142 (and_142_out, not_14_out, add_12_s, not_12_out, not_10_out);
  and and_143 (and_143_out, not_14_out, add_12_s, not_11_out, not_10_out);
  and and_144 (and_144_out, not_14_out, not_13_out, add_4_s, not_10_out);
  and and_145 (and_145_out, not_14_out, not_13_out, not_11_out, add_1_s);
  and and_146 (and_146_out, not_14_out, add_12_s, add_8_s, not_10_out);
  and and_147 (and_147_out, not_14_out, add_12_s, add_4_s, not_10_out);
  and and_148 (and_148_out, not_14_out, not_13_out, not_11_out, add_1_s);
  and and_149 (and_149_out, not_13_out, add_8_s, not_11_out, not_10_out);
  and and_150 (and_150_out, not_13_out, not_12_out, add_4_s, not_10_out);
  and and_151 (and_151_out, add_12_s, add_8_s, add_4_s, not_10_out);
  and and_152 (and_152_out, add_12_s, not_12_out, not_11_out, add_1_s);
  and and_153 (and_153_out, not_14_out, add_12_s, not_11_out, not_10_out);
  and and_154 (and_154_out, not_14_out, not_12_out, not_11_out, add_1_s);
  and and_155 (and_155_out, add_12_s, not_12_out, not_11_out);
  and and_156 (and_156_out, not_13_out, add_8_s, not_10_out);
  and and_157 (and_157_out, not_13_out, add_4_s, not_10_out);
  and and_158 (and_158_out, add_8_s, add_4_s, not_10_out);
  or or_24 (or_24_out, and_88_out, and_89_out, and_90_out, and_91_out);
  or or_25 (or_25_out, and_92_out, and_93_out, and_94_out, and_95_out, and_96_out);
  or or_26 (or_26_out, and_97_out, and_98_out, and_99_out, and_100_out, and_101_out);
  or or_27 (or_27_out, and_102_out, and_103_out, and_104_out, and_105_out);
  or or_28 (or_28_out, and_106_out, and_107_out, and_108_out, and_109_out);
  or or_29 (or_29_out, and_110_out, and_111_out, and_112_out, and_113_out);
  or or_30 (or_30_out, and_128_out, and_129_out, and_130_out, and_131_out, and_132_out);
  or or_31 (or_31_out, and_141_out, and_142_out, and_143_out, and_144_out, and_145_out);
  or or_32 (or_32_out, and_115_out, and_116_out, and_117_out, and_118_out, and_119_out, and_120_out);
  or or_33 (or_33_out, and_121_out, and_122_out, and_123_out, and_124_out, and_125_out, and_126_out, and_127_out);
  or or_34 (or_34_out, and_133_out, and_134_out, and_135_out, and_136_out, and_137_out, and_138_out, and_139_out, and_140_out);
  or or_35 (or_35_out, and_146_out, and_147_out, and_148_out, and_149_out, and_150_out, and_151_out, and_152_out);
  or or_36 (or_36_out, and_153_out, and_154_out, and_155_out, and_156_out, and_157_out, and_158_out);
  and and_159 (and_159_out, or_19_out, D3_0_q);
  and and_160 (and_160_out, or_20_out, D3_1_q);
  and and_161 (and_161_out, or_21_out, D3_2_q);
  and and_162 (and_162_out, C_3_4_p15, D3_3_q);
  and and_163 (and_163_out, or_19_out, D2_0_q);
  and and_164 (and_164_out, or_20_out, D2_1_q);
  and and_165 (and_165_out, or_21_out, D2_2_q);
  and and_166 (and_166_out, C_3_4_p15, D2_3_q);
  and and_167 (and_167_out, or_19_out, D1_0_q);
  and and_168 (and_168_out, or_20_out, D1_1_q);
  and and_169 (and_169_out, or_21_out, D1_2_q);
  and and_170 (and_170_out, C_3_4_p15, D1_3_q);
  and and_171 (and_171_out, or_19_out, D0_0_q);
  and and_172 (and_172_out, or_21_out, D0_1_q);
  and and_173 (and_173_out, or_21_out, D0_2_q);
  and and_174 (and_174_out, C_3_4_p15, D0_3_q);
  xor xor_1 (xor_1_out, ~and_175_out, or_16_out);  // XOr
  and and_175 (and_175_out, ~or_39_out, ~or_37_out, or_40_out, or_38_out);  // And
  not not_15 (not_15_out, or_37_out);
  not not_16 (not_16_out, or_38_out);
  not not_17 (not_17_out, or_39_out);
  not not_18 (not_18_out, or_40_out);
  not not_19 (not_19_out, D3_0_2_q);
  not not_20 (not_20_out, D2_0_2_q);
  not not_21 (not_21_out, D1_0_2_q);
  or or_37 (or_37_out, and_159_out, and_160_out, and_161_out, and_162_out);
  or or_38 (or_38_out, and_163_out, and_164_out, and_165_out, and_166_out);
  or or_39 (or_39_out, and_167_out, and_168_out, and_169_out, and_170_out);
  or or_40 (or_40_out, and_171_out, and_172_out, and_173_out, and_174_out);
  not not_22 (not_22_out, D0_0_2_q);
  and and_176 (and_176_out, not_22_out, not_21_out, D2_0_2_q, not_19_out, not_18_out, not_17_out, or_38_out, not_15_out);
  and and_177 (and_177_out, D0_0_2_q, D1_0_2_q, D2_0_2_q, not_19_out, not_18_out, or_38_out, not_15_out);
  and and_178 (and_178_out, D0_0_2_q, not_20_out, not_19_out, or_40_out, or_39_out, not_16_out, not_15_out);
  and and_179 (and_179_out, D0_0_2_q, not_21_out, not_20_out, not_18_out, or_38_out, not_15_out);
  and and_180 (and_180_out, not_22_out, D1_0_2_q, not_20_out, or_39_out, not_16_out, not_15_out);
  and and_181 (and_181_out, not_22_out, not_20_out, D3_0_2_q, not_18_out, or_38_out, not_15_out);
  and and_182 (and_182_out, D0_0_2_q, not_21_out, not_20_out, or_39_out, not_15_out);
  and and_183 (and_183_out, D1_0_2_q, not_20_out, not_19_out, not_18_out, not_17_out, or_38_out, not_15_out);
  and and_184 (and_184_out, not_21_out, not_20_out, D3_0_2_q, or_39_out, not_15_out);
  and and_185 (and_185_out, D0_0_2_q, not_21_out, not_20_out, D3_0_2_q, or_40_out, or_39_out, or_38_out, not_15_out);
  and and_186 (and_186_out, D0_0_2_q, not_21_out, not_20_out, not_19_out, or_40_out, not_17_out, not_16_out, or_37_out);
  and and_187 (and_187_out, D0_0_2_q, D1_0_2_q, D2_0_2_q, not_19_out, or_40_out, not_17_out, not_16_out, or_37_out);
  and and_188 (and_188_out, not_22_out, D1_0_2_q, not_20_out, D3_0_2_q, or_40_out, not_17_out, not_16_out, or_37_out);
  and and_189 (and_189_out, D0_0_2_q, not_21_out, D2_0_2_q, not_19_out, not_18_out, not_17_out, or_38_out, not_15_out);
  and and_190 (and_190_out, not_22_out, D1_0_2_q, D2_0_2_q, not_19_out, not_18_out, not_17_out, or_38_out, not_15_out);
  and and_191 (and_191_out, D0_0_2_q, not_21_out, not_20_out, D3_0_2_q, or_40_out, or_39_out, or_38_out, not_15_out);
  and and_192 (and_192_out, not_22_out, not_21_out, not_20_out, D3_0_2_q, or_40_out, or_39_out, not_15_out);
  and and_193 (and_193_out, D0_0_2_q, not_21_out, not_20_out, not_18_out, not_17_out, not_16_out, or_37_out);
  and and_194 (and_194_out, not_22_out, not_20_out, D3_0_2_q, not_18_out, not_17_out, not_16_out, or_37_out);
  and and_195 (and_195_out, not_22_out, D2_0_2_q, not_19_out, or_40_out, not_17_out, not_16_out);
  and and_196 (and_196_out, not_22_out, D2_0_2_q, not_19_out, not_18_out, or_38_out, not_15_out);
  and and_197 (and_197_out, D0_0_2_q, not_19_out, or_40_out, not_17_out, not_16_out, not_15_out);
  and and_198 (and_198_out, D1_0_2_q, not_20_out, not_19_out, or_40_out, not_17_out, not_16_out);
  and and_199 (and_199_out, not_21_out, not_20_out, D3_0_2_q, or_40_out, not_17_out, not_16_out);
  and and_200 (and_200_out, not_21_out, D2_0_2_q, not_19_out, not_18_out, or_38_out, not_15_out);
  and and_201 (and_201_out, not_21_out, D2_0_2_q, not_19_out, not_17_out, not_16_out, or_37_out);
  and and_202 (and_202_out, D1_0_2_q, not_19_out, not_18_out, not_17_out, not_16_out, or_37_out);
  and and_203 (and_203_out, D1_0_2_q, not_19_out, or_39_out, not_15_out);
  and and_204 (and_204_out, D2_0_2_q, not_19_out, or_39_out, not_15_out);
  or or_41 (or_41_out, and_185_out, and_186_out, and_187_out, and_188_out);
  or or_42 (or_42_out, and_189_out, and_190_out);
  or or_43 (or_43_out, and_176_out, and_177_out, and_178_out, and_179_out, and_180_out, and_181_out, and_182_out, and_183_out, and_184_out);
  or or_44 (or_44_out, and_192_out, and_193_out, and_194_out, and_195_out, and_196_out, and_197_out, and_198_out, and_199_out, and_200_out, and_201_out, and_202_out, and_203_out, and_204_out);

  // Notes on the sheet:
  //   Reset_Pulse: Hz: 50000
endmodule
